# Fritzing sketch Reptile-inator (saved by Fritzing 0.9.3b)
breadboards: 1

parts:
  Part1 = Arduino Nano (Rev3.0)
  ZS-042_RTC1 = ZS-042 RTC Module
  Grove1 = Grove OLED 128x96
  RHT1 = Humidity and Temperature Sensor RHT03
  RHT2 = Humidity and Temperature Sensor RHT03
  R1 = Resistor [tolerance=±5% resistance=10k package=THT]
  R2 = Resistor [tolerance=±5% resistance=10k package=THT]
  Q1 = Basic FET N-Channel [package="D2Pak [SMD]"]
  Q2 = Basic FET N-Channel [package="D2Pak [SMD]"]
  Q3 = Basic FET N-Channel [package="D2Pak [SMD]"]
  LED1 = RGB LED - (4 legs) [package="5 mm [THT]"]
  R3 = Resistor [tolerance=±5% resistance=10k package=THT]

nets:
  N1: Part1.D2, RHT2.Data-signal
  N2: Part1.D3, Q1.Gate, R3.Pin_1
  N3: Part1.D4, RHT1.Data-signal
  N4: Part1.D5, R2.Pin_1, Q2.Gate
  N5: Part1.D6, R1.Pin_1, Q3.Gate
  N6: Part1.A5, ZS-042_RTC1.SCL, Grove1.SCL
  N7: Part1.A4, ZS-042_RTC1.SDA, Grove1.SDA
  GND: ZS-042_RTC1.GND, Grove1.GND
  VCC: ZS-042_RTC1.VCC, Grove1.VCC
  N8: RHT1.Vcc, RHT1.GND_2, RHT2.GND_2, R1.Pin_0, R2.Pin_0, Q1.source, Q2.source, Q3.source, R3.Pin_0
  N9: RHT2.Vcc, LED1.common_anode
  N10: Q1.drain, LED1.red_cathode
  N11: Q2.drain, LED1.green_cathode
  N12: Q3.drain, LED1.blue_cathode
